# Fritzing sketch 28BYJ-48_and_ULN2003 (saved by Fritzing 0.9.3b)

parts:
  MOTOR1 = 28BYJ-48 Stepper Motor  # not connected
  BREAKOUT1 = ULN2003A breakout board
  Raspberry_Pi_1 = Raspberry Pi 4 [part_number=RPI-4-b]
  Power_plug1 = Power plug

nets:
  N1: BREAKOUT1.In_1, Raspberry_Pi_1.GPIO17
  N2: BREAKOUT1.In_2, Raspberry_Pi_1.GPIO18
  N3: BREAKOUT1.In_3, Raspberry_Pi_1.GPIO27
  N4: BREAKOUT1.In_4, Raspberry_Pi_1.GPIO22
  N5: BREAKOUT1.0V, Power_plug1.GND
  +5V: BREAKOUT1.+5V, Power_plug1.VCC

notes:
  5V to 12V
  5V

custom parts:
  ULN2003A breakout board: ULN2003A 7-way Darlington Transistor Driver on breakoutboard
  Raspberry Pi 4: The RPi4, a faster version of the awesome Raspberry Pi 2 B ARM Board with 40 pin gpio. Ready for special Raspberry Pi B+ and RPi2 Hat (Hardware attached (on) top)
